// Logisim project Osciloscopio.circ as structural Verilog: 2 circuits, main circuit Osciloscópio
module \Osciloscópio  (
  input  A,
  input  B,
  input  C,
  input  Clock,
  input  Enable
);

  wire and_1_out, and_2_out, and_3_out, and_4_out, Clear_out, not_1_out, not_2_out, or_1_out, or_2_out;

  not not_1 (not_1_out, B);
  not not_2 (not_2_out, A);
  and and_1 (and_1_out, not_2_out, C);
  and and_2 (and_2_out, B, C);
  and and_3 (and_3_out, A, not_1_out);
  and and_4 (and_4_out, A, C);
  or or_1 (or_1_out, and_1_out, and_2_out);
  or or_2 (or_2_out, and_3_out, and_4_out);
  Button Clear (.out(Clear_out));
  // Digital_Oscilloscope Osciloscópio: pin names not known; wires that end beside it: Clock, or_1_out, or_2_out, Enable, Clear_out
endmodule

module Clock (
  input  in_1
);

  wire clock_1_out, clock_2_out, clock_3_out;

  Clock_part clock_1 (.out(clock_1_out));
  Clock_part #(.highDuration(2), .lowDuration(2)) clock_2 (.out(clock_2_out));
  Clock_part #(.highDuration(3), .lowDuration(3)) clock_3 (.out(clock_3_out));
  // Digital_Oscilloscope digital_oscilloscope_1: pin names not known; wires that end beside it: clock_1_out, clock_2_out, clock_3_out, in_1
endmodule
